# Fritzing sketch circuit 2 (saved by Fritzing 0.9.3b)

parts:
  Part1 = Arduino Uno (Rev3)
  Part2 = Bluetooth HC-05 Macho
  U1 = 4-Channel 5v Relay Shield [package=relay-4ch5v10a]
  U2 = 4-Channel 5v Relay Shield [package=relay-4ch5v10a]

nets:
  N1: Part1.D8, U1.IN4
  N2: Part1.D9_PWM, U1.IN3
  N3: Part1.D10_PWM/SS, U1.IN2
  N4: Part1.D11_PWM/MOSI, U1.IN1
  GND: Part1.GND, U1.GND, U2.GND
  N5: Part1.D2, Part2.TXD
  N6: Part1.D3_PWM, Part2.RXD
  N7: Part1.D4, U2.IN4
  N8: Part1.D5_PWM, U2.IN3
  N9: Part1.D6_PWM, U2.IN2
  N10: Part1.D7, U2.IN1
  5V: Part1.5V, U1.VCC

custom parts:
  4-Channel 5v Relay Shield: 4 Channel 5v Relay Shield w. 2x SPD-06VDC-SD-C
